# Fritzing sketch wiring_diagram_nct (saved by Fritzing 0.9.3b)
breadboards: 1

parts:
  Part2 = TFT 1.8 inch 160x128 w microSD [part_number=358]
  Part1 = Itsy Bitsy 32u4 3V @ 8MHz [part_number="Adafruit 3675"]
  Part3 = NeoPixel Jewel [part_number=2226]
  J1 = female pin header, 8 pins [form="♀ (female)" part_number="8 pin header"]
  J3 = female pin header, 3 pins [form="♀ (female)" part_number="3-pin header"]
  J5 = female pin header, 5 pins [form="♀ (female)" part_number="5-pin header"]
  J9 = female pin header, 5 pins [form="♀ (female)" part_number="5-pin header"]
  J10 = female pin header, 8 pins [form="♀ (female)" part_number="8 pin header"]
  J11 = female pin header, 3 pins [form="♀ (female)" part_number="3-pin header"]
  J12 = female pin header, 5 pins [form="♀ (female)" part_number="5-pin header"]
  S1 = SWITCH-MOMENTARY-2 [package=tactile-pth-12mm]
  S2 = SWITCH-MOMENTARY-2 [package=tactile-pth-12mm]
  S3 = SWITCH-MOMENTARY-2 [package=tactile-pth-12mm]
  S4 = SWITCH-MOMENTARY-2 [package=tactile-pth-12mm]
  R1 = Rotary Potentiometer (Large) [maximum_resistance=100kΩ package=THT]
  R2 = Rotary Potentiometer (Large) [maximum_resistance=100kΩ package=THT]
  R3 = Rotary Potentiometer (Large) [maximum_resistance=100kΩ package=THT]
  J13 = female pin header, 5 pins [form="♀ (female)" part_number="5-pin header"]
  Part4 = Adafruit Micro USB Breakout [part_number="Adafruit #1833"]
  R4 = Resistor [tolerance=±5% resistance=470 package=THT]

nets:
  N1: Part2.LITE, J10.pin8
  N2: Part2.SCLK, J10.pin7
  N3: Part2.MOSI, J10.pin6
  N4: Part2.TFTCS, J10.pin5
  N5: Part2.TFTDC, J10.pin4
  N6: Part2.RESET, J10.pin3
  N7: Part2.+5V, J10.pin2
  N8: Part2.GND, J10.pin1
  GND: Part1.GND, J1.pin1, J3.pin3, J5.pin5, J9.pin2, Part4.GND
  N9: Part1.VBUS, Part4.VBUS
  N10: Part1.D12, J5.pin4
  N11: Part1.D11, J5.pin3
  N12: Part1.D10, J1.pin5
  N13: Part1.D9, J1.pin3
  N14: Part1.D7, J1.pin4
  N15: Part1.D5_OUT, R4.Pin_0
  N16: Part1.D1, J5.pin2
  N17: Part1.D0, J5.pin1
  N18: Part1.MOSI, J1.pin6
  N19: Part1.SCK, J1.pin7
  N20: Part1.A2, J9.pin5
  N21: Part1.A1, J9.pin4
  N22: Part1.A0, J9.pin3
  N23: Part1.VMAX, J3.pin2
  N24: Part1.+3V3, J1.pin2, J1.pin8, J9.pin1
  N25: Part3.GND, J11.pin3
  N26: Part3.IN, J11.pin1
  N27: Part3.VDD, J11.pin2
  N28: J3.pin1, R4.Pin_1
  N29: J12.pin1, S4.2
  N30: J12.pin2, S3.2
  N31: J12.pin3, S2.2
  N32: J12.pin4, S1.2
  N33: J12.pin5, S1.1, S2.1, S3.1, S4.1
  N34: R1.leg1, R2.leg1, R3.leg1, J13.pin2
  N35: R1.wiper, J13.pin5
  N36: R1.leg2, R2.leg2, R3.leg2, J13.pin1
  N37: R2.wiper, J13.pin3
  N38: R3.wiper, J13.pin4

custom parts:
  TFT 1.8 inch 160x128 w microSD: This lovely little display breakout is the best way to add a small, colorful and bright display to any project. Since the display uses 4-wire SPI to communicate and has its own pixel-addressable frame buffer, it can be used with every kind of microcontroller. Even a very small one with low memory and few pins available! The 1.8" display has 128x160 color pixels.
  Itsy Bitsy 32u4 3V @ 8MHz: What's smaller than a Feather but larger than a Trinket? It's an Itsy Bitsy! Small, powerful, Arduino-compatible - this microcontroller board is perfect when you want something very compact, but still with a bunch of pins. Itsy Bitsy is only 1.4" long by 0.7" wide, but has 6 power pins, 6 analog & digital pins and 17 digital pins. It packs much of the same capability as an Arduino UNO or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
  NeoPixel Jewel: We fit seven of our tiny 5050 (5mm x 5mm) smart RGB LEDs onto a beautiful, round PCB with mounting holes and a chainable design to create what we think is our most elegant (and evening-wear appropriate) NeoPixel board yet. Use only one microcontroller pin to control as many as you can chain together! Each LED is addressable as the driver chip is inside the LED. Each one has ~18mA constant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
  Adafruit Micro USB Breakout: Simple but effective - this breakout board has a USB Micro-B connector, with all 5 pins broken out. Great for pairing with a microcontroller with USB support, or adding USB 5V power to a project. We use a micro-AB connector with through-hole shielding pads for an excellent strong connection - it won't rip off by accident! Comes with one fully assembled and tested micro B breakout PCB and a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
